# Fritzing sketch ESP32_radio (saved by Fritzing 0.9.3b)
circuit board: 7.82958cm x 4.56853cm
breadboards: 1

parts:
  SP2 = SPEAKER [package=pcb_mount_speaker]
  VS1053B2 = VS1053B
  AMP1 = GF1002 Stereo Amplifier
  M1 = DOIT Esp32 DevKit v1 (30 pins long, 11 pins width) [part_number=ESP32S-PIN30]
  TFT1 = Color 320x240 TFT Display, ILI9341 Controller Chip
  R1 = Trimmer Potentiometer [maximum_resistance=10kΩ package=THT]
  C1 = Ceramic Capacitor [capacitance=100nF package="100 mil [THT, multilayer]"]
  C2 = Ceramic Capacitor [capacitance=100nF package="100 mil [THT, multilayer]"]
  RE1 = Rotary Encoder [package=THT]
  S1 = Pushbutton [package=THT]
  C3 = Ceramic Capacitor [capacitance=100nF package="100 mil [THT, multilayer]"]
  U1 = Transformer [part_number=600:600 package=transformer]
  J_AUD_IN = male pin header, 3 pins [form="♂ (male)"]
  R9 = Resistor [tolerance=±5% resistance=3.3k package=THT]
  R10 = Resistor [tolerance=±5% resistance=3.3k package=THT]
  J_AUD_OUT2 = male pin header, 2 pins [form="♂ (male)"]
  J_AUD_OUT1 = male pin header, 2 pins [form="♂ (male)"]
  J_sdi = male pin header, 2 pins [form="♂ (male)"]
  J_reset = male pin header, 3 pins [form="♂ (male)"]
  S2 = SPST Switch [package=switch-spdt_kit]
  J_pwr = screw terminal, 2 pins
  j_2 = male pin header, 1 pin [form="♂ (male)"]
  j_tft2 = double row male pin header, 6 pins [form="♂ (male)"]
  j_vs3 = male pin header, 2 pins [form="♂ (male)"]
  j_tft4 = male pin header, 1 pin [form="♂ (male)"]
  J_dc = male pin header, 2 pins [form="♂ (male)"]
  j_pow = double row male pin header, 6 pins [form="♂ (male)"]
  R8 = Resistor [tolerance=±5% resistance=10k package="0805 [SMD]"]
  R2 = Resistor [tolerance=±5% resistance=10k package="0805 [SMD]"]
  R7 = Resistor [tolerance=±5% resistance=10k package="0805 [SMD]"]
  R3 = Resistor [tolerance=±5% resistance=10k package="0805 [SMD]"]
  R6 = Resistor [tolerance=±5% resistance=1k package="0805 [SMD]"]
  J_enc = male pin header, 1 pin [form="♂ (male)"]
  J_enc2 = male pin header, 2 pins [form="♂ (male)"]

nets:
  N1: SP2.+, AMP1.LOUT-
  N2: SP2.-, AMP1.LOUT+
  GND: VS1053B2.Gnd, M1.GND, TFT1.GND, C1.0, C2.0, RE1.EncoderPinC, S1.leg0, C3.0, J_pwr.pin2, j_pow.pin4, j_pow.pin5, j_pow.pin6
  N3: VS1053B2.XCS, M1.D32, j_vs3.pin1
  N4: VS1053B2.XDCS, M1.D33, TFT1.D/C, J_dc.pin1, J_dc.pin2
  N5: VS1053B2.DREQ, M1.D35, j_vs3.pin2
  N6: VS1053B2.MOSI, M1.D23, TFT1.SDI_(MOSI), J_sdi.pin1, J_sdi.pin2
  N7: VS1053B2.SCK, M1.D18, TFT1.SCK, j_tft2.pin2, j_tft2.pin5
  N8: VS1053B2.MISO, M1.D19, TFT1.SDO_(MISO), j_tft2.pin3, j_tft2.pin4
  N9: VS1053B2.XRST, M1.EN, TFT1.Reset, J_reset.pin1, J_reset.pin2, J_reset.pin3
  N10: AMP1.INPUTL, U1.4, J_AUD_OUT2.pin2
  N11: AMP1.INPUTG, U1.3, J_AUD_OUT2.pin1
  3.3V: M1.3V3, TFT1.VCC, R1.leg2, j_pow.pin1, j_pow.pin2, j_pow.pin3, R8.Pin_0, R7.Pin_0
  GPIO15: M1.D15, C3.1, R6.Pin_0
  GPIO16: M1.RX2, C1.1, R3.Pin_1
  GPIO17: M1.TX2, C2.1, R2.Pin_0
  N12: M1.D5, j_tft2.pin1, j_tft2.pin6
  N13: M1.D27, TFT1.CS, j_tft4.pin1
  N14: M1.VIN, J_pwr.pin1
  N15: TFT1.LED, R1.wiper, j_2.pin1
  N16: RE1.EncoderPinA, R8.Pin_1, R3.Pin_0, J_enc2.pin1
  N17: RE1.EncoderPinB, R2.Pin_1, R7.Pin_1, J_enc2.pin2
  N18: S1.leg1, R6.Pin_1, J_enc.pin1
  N19: U1.1, S2.O
  N20: U1.2, J_AUD_IN.pin1, J_AUD_OUT1.pin1
  N21: J_AUD_IN.pin2, R10.Pin_0
  N22: J_AUD_IN.pin3, R9.Pin_0
  N23: R9.Pin_1, R10.Pin_1, S2.P
  N24: J_AUD_OUT1.pin2, S2.S

custom parts:
  VS1053B: VS1053B module
  GF1002 Stereo Amplifier: GF1002 6 Watt Stereo Amplifier
  DOIT Esp32 DevKit v1 (30 pins long, 11 pins width): The DOIT Esp32 DevKit v1 is one of the development board created by DOIT to evaluate the ESP-WROOM-32 module. It is based on the ESP32 microcontroller that boasts Wifi, Bluetooth, Ethernet and Low Power support all in a single chip. (vanepp) made breadboard work, adjusted pin numbering and labels and reduced size of schematic and cleaned up pcb. This chip is 30pins long (2 x15) and 11 pins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
  Color 320x240 TFT Display, ILI9341 Controller Chip: 2.2" TFT Display with ILI9341 Controller
